// Logisim project 150119692_150119860_150119766_170517033.circ as structural Verilog: 18 circuits, main circuit main
module main (
  input  Reset,
  input  Jump,
  input  DataMem_Clear,
  input  External_Reset,
  input  Regiset_Reset,
  output [17:0] Instruction,
  output Reset_State,
  output [17:0] ALU_Output
);

  wire ALU_Enable, and_1_out, Br_Enable, branch_1_branchout, clock_1_out, DataMem_Read, DatMem_Write,
       Fetch_Inst, Jmp_Enable, Load_Active, or_1_out, PC_Read, PC_Write, Register_Read, Register_Write,
       Select_IMM;
  wire [2:0] NZP;
  wire [3:0] DSR, Operation_Select, SR1_OP1, SR2_OP2;
  wire [5:0] IMM6;
  wire [17:0] ADDR, ALU_Result, DataMem_Result, multiplexer_1_out, programcounter_1_out, ram_1_data,
       registers_1_src1_2, registers_1_src2_2, signextender6_1_signextended, SRC1, SRC2;

  Clock clock_1 (.out(clock_1_out));
  SignExtender6 signextender6_1 (.\İnput (IMM6), .SignExtended(signextender6_1_signextended));
  Branch branch_1 (.nzp(NZP), .OP1(SRC1), .OP2(SRC2), .BranchOut(branch_1_branchout));
  or or_1 (or_1_out, Jump, Jmp_Enable, and_1_out);
  and and_1 (and_1_out, branch_1_branchout, Br_Enable);
  ProgramCounter programcounter_1 (
    .PCWrite(or_1_out), .Reset(Reset), .PC_Read(PC_Read), .Clk(clock_1_out), .JmpAddress(ADDR),
    .Out(programcounter_1_out));  // open: CarryOut
  ALU alu_1 (
    .SR1(SRC1), .SR2(SRC2), .IMM(signextender6_1_signextended), .Select(Select_IMM),
    .ALU_Select(Operation_Select), .out_6(ALU_Output));
  Register #(.width(18)) register_1 (.D(ALU_Output), .Q(ALU_Result), .clk(clock_1_out));  // open: en, clr
  ROM #(.addrWidth(18), .dataWidth(18)) rom_1 (.addr(programcounter_1_out), .data(Instruction));  // open: sel
  Control_Unit control_unit_1 (
    .CounterReset(External_Reset), .Clock(clock_1_out), .Instruction(Instruction), .IMM6(IMM6),
    .SR2_OP2(SR2_OP2), .DSR(DSR), .SR1_OP1(SR1_OP1), .NZP(NZP), .ADDR(ADDR), .Load_Active(Load_Active),
    .Jmp_Enable(Jmp_Enable), .Br_Enable(Br_Enable), .PC_Read(PC_Read), .Fetch_Inst(Fetch_Inst),
    .Register_Read(Register_Read), .DataMem_Read(DataMem_Read), .PC_Write(PC_Write), .ALU_Enable(ALU_Enable),
    .Register_Write(Register_Write), .DataMem_Write(DatMem_Write), .Select_IMM(Select_IMM),
    .Operation_Select(Operation_Select), .Reset_State(Reset_State));
  Multiplexer #(.width(18), .enable("false")) multiplexer_1 (
    .in0(ALU_Result), .in1(DataMem_Result), .out(multiplexer_1_out), .sel(Load_Active));
  Registers registers_1 (
    .Input_Data(multiplexer_1_out), .DST(DSR), .Load(Register_Write), .Clock(clock_1_out),
    .SRC1_2(registers_1_src1_2), .Src1(SR1_OP1), .SRC2_2(registers_1_src2_2), .Src2(SR2_OP2),
    .Reset(Regiset_Reset));
  Register #(.width(18)) register_2 (
    .D(registers_1_src1_2), .en(Register_Read), .Q(SRC1), .clk(clock_1_out));  // open: clr
  Register #(.width(18)) register_3 (
    .D(registers_1_src2_2), .en(Register_Read), .Q(SRC2), .clk(clock_1_out));  // open: clr
  Register #(.width(18)) register_4 (.D(ram_1_data), .Q(DataMem_Result), .clk(clock_1_out));  // open: en, clr
  RAM #(.addrWidth(18), .dataWidth(18), .bus("separate")) ram_1 (
    .addr(ADDR), .din(SRC1), .data(ram_1_data), .str(DatMem_Write), .clk(clock_1_out), .ld(DataMem_Read),
    .clr(DataMem_Clear));  // open: sel

  // Notes on the sheet:
  //   Yasin Alper Bingül 170517033
  //   Onur Kaya 150119860
  //   Bedirhan Sarıhan 150119692
  //   Emre Sağıroğlu 150119766
  //   CSE3015 - DIGITAL LOGIC DESIGN TERM PROJECT
  //   contents of rom_1 (hex, n*v repeats v):
  //   0 1c403 4840 10800 c000 2c842 28009 21881 1dc47 2e5f1 11c01
endmodule

module _1_FA (
  input  C_in,
  input  Input_1,
  input  Input_2,
  output Sum,
  output C_out
);

  wire and_1_out, and_2_out, and_3_out;

  xor xor_1 (Sum, C_in, Input_1, Input_2);
  and and_1 (and_1_out, C_in, Input_1);
  and and_2 (and_2_out, C_in, Input_2);
  and and_3 (and_3_out, Input_1, Input_2);
  or or_1 (C_out, and_1_out, and_2_out, and_3_out);
endmodule

module _1_HA (
  input  Input_1,
  input  Input_2,
  output Sum,
  output C_out
);

  xor xor_1 (Sum, Input_1, Input_2);
  and and_1 (C_out, Input_1, Input_2);
endmodule

// Add
module _18bitAdder (
  input  [17:0] Input1,
  input  [17:0] Input2,
  output [17:0] Sum_Out,
  output C_out
);

  wire n1_fa_1_c_out, n1_fa_2_c_out, n1_fa_3_c_out, n1_fa_4_c_out, n1_fa_5_c_out, n1_fa_6_c_out,
       n1_fa_7_c_out, n1_fa_8_c_out, n1_fa_9_c_out, n1_fa_10_c_out, n1_fa_11_c_out, n1_fa_12_c_out,
       n1_fa_13_c_out, n1_fa_14_c_out, n1_fa_15_c_out, n1_fa_16_c_out, n1_ha_1_c_out;

  _1_HA u_1_ha_1 (.Input_1(Input1[0]), .Input_2(Input2[0]), .Sum(Sum_Out[0]), .C_out(n1_ha_1_c_out));
  _1_FA u_1_fa_1 (
    .C_in(n1_ha_1_c_out), .Input_1(Input1[1]), .Input_2(Input2[1]), .Sum(Sum_Out[1]), .C_out(n1_fa_1_c_out));
  _1_FA u_1_fa_2 (
    .C_in(n1_fa_1_c_out), .Input_1(Input1[2]), .Input_2(Input2[2]), .Sum(Sum_Out[2]), .C_out(n1_fa_2_c_out));
  _1_FA u_1_fa_3 (
    .C_in(n1_fa_2_c_out), .Input_1(Input1[3]), .Input_2(Input2[3]), .Sum(Sum_Out[3]), .C_out(n1_fa_3_c_out));
  _1_FA u_1_fa_4 (
    .C_in(n1_fa_3_c_out), .Input_1(Input1[4]), .Input_2(Input2[4]), .Sum(Sum_Out[4]), .C_out(n1_fa_4_c_out));
  _1_FA u_1_fa_5 (
    .C_in(n1_fa_4_c_out), .Input_1(Input1[5]), .Input_2(Input2[5]), .Sum(Sum_Out[5]), .C_out(n1_fa_5_c_out));
  _1_FA u_1_fa_6 (
    .C_in(n1_fa_5_c_out), .Input_1(Input1[6]), .Input_2(Input2[6]), .Sum(Sum_Out[6]), .C_out(n1_fa_6_c_out));
  _1_FA u_1_fa_7 (
    .C_in(n1_fa_6_c_out), .Input_1(Input1[7]), .Input_2(Input2[7]), .Sum(Sum_Out[7]), .C_out(n1_fa_7_c_out));
  _1_FA u_1_fa_8 (
    .C_in(n1_fa_7_c_out), .Input_1(Input1[8]), .Input_2(Input2[8]), .Sum(Sum_Out[8]), .C_out(n1_fa_8_c_out));
  _1_FA u_1_fa_9 (
    .C_in(n1_fa_8_c_out), .Input_1(Input1[9]), .Input_2(Input2[9]), .Sum(Sum_Out[9]), .C_out(n1_fa_9_c_out));
  _1_FA u_1_fa_10 (
    .C_in(n1_fa_9_c_out), .Input_1(Input1[10]), .Input_2(Input2[10]), .Sum(Sum_Out[10]),
    .C_out(n1_fa_10_c_out));
  _1_FA u_1_fa_11 (
    .C_in(n1_fa_10_c_out), .Input_1(Input1[11]), .Input_2(Input2[11]), .Sum(Sum_Out[11]),
    .C_out(n1_fa_11_c_out));
  _1_FA u_1_fa_12 (
    .C_in(n1_fa_11_c_out), .Input_1(Input1[12]), .Input_2(Input2[12]), .Sum(Sum_Out[12]),
    .C_out(n1_fa_12_c_out));
  _1_FA u_1_fa_13 (
    .C_in(n1_fa_12_c_out), .Input_1(Input1[13]), .Input_2(Input2[13]), .Sum(Sum_Out[13]),
    .C_out(n1_fa_13_c_out));
  _1_FA u_1_fa_14 (
    .C_in(n1_fa_13_c_out), .Input_1(Input1[14]), .Input_2(Input2[14]), .Sum(Sum_Out[14]),
    .C_out(n1_fa_14_c_out));
  _1_FA u_1_fa_15 (
    .C_in(n1_fa_14_c_out), .Input_1(Input1[15]), .Input_2(Input2[15]), .Sum(Sum_Out[15]),
    .C_out(n1_fa_15_c_out));
  _1_FA u_1_fa_16 (
    .C_in(n1_fa_15_c_out), .Input_1(Input1[16]), .Input_2(Input2[16]), .Sum(Sum_Out[16]),
    .C_out(n1_fa_16_c_out));
  _1_FA u_1_fa_17 (.C_in(n1_fa_16_c_out), .Input_1(Input1[17]), .Input_2(Input2[17]), .Sum(Sum_Out[17]), .C_out(C_out));
endmodule

module ALU (
  input  [17:0] SR1,
  input  [17:0] SR2,
  input  [17:0] IMM,
  input  Select,
  input  [3:0] ALU_Select,
  output [17:0] out_6
);

  wire n18bitadder_1_c_out;
  wire [17:0] and_1_out, multiplexer_1_out, n18bitadder_1_sum_out, or_1_out, xor_1_out;

  Multiplexer #(.width(18), .enable("false")) multiplexer_1 (
    .in0(SR2), .in1(IMM), .out(multiplexer_1_out), .sel(Select));
  _18bitAdder u_18bitadder_1 (
    .Input1(SR1), .Input2(multiplexer_1_out), .Sum_Out(n18bitadder_1_sum_out), .C_out(n18bitadder_1_c_out));
  assign xor_1_out = SR1 ^ multiplexer_1_out;  // XOR_Gate xor_1, 18 bits wide
  assign or_1_out = SR1 | multiplexer_1_out;  // OR_Gate or_1, 18 bits wide
  assign and_1_out = SR1 & multiplexer_1_out;  // AND_Gate and_1, 18 bits wide
  Multiplexer #(.select(4), .width(18), .enable("false")) multiplexer_2 (
    .in1(n18bitadder_1_sum_out), .in2(xor_1_out), .in4(or_1_out), .in7(and_1_out), .out(out_6),
    .sel(ALU_Select));  // open: in0, in3, in5, in6, in8, in9, in10, in11, in12, in13, in14, in15
  // also tied to GND on the sheet: n18bitadder_1_c_out
endmodule

// Bra
module Branch (
  input  [2:0] nzp,
  input  [17:0] OP1,
  input  [17:0] OP2,
  output BranchOut
);

  wire and_1_out, and_2_out, and_3_out, and_4_out, and_5_out, and_6_out, and_7_out, decoder_1_out1,
       decoder_1_out2, decoder_1_out3, decoder_1_out4, decoder_1_out6, decoder_2_out1, decoder_2_out2,
       decoder_2_out4, or_1_out, or_2_out;
  wire [2:0] n18bitscomparator_1_out;

  _18BitsComparator u_18bitscomparator_1 (
    .A(OP1), .B(OP2), .Out(n18bitscomparator_1_out));  // open: eq_out, gt_out, lt_out
  Decoder #(.select(3), .enable("false")) decoder_1 (
    .out1(decoder_1_out1), .out2(decoder_1_out2), .out3(decoder_1_out3), .out4(decoder_1_out4),
    .out6(decoder_1_out6), .sel(nzp));  // open: out0, out5, out7
  Decoder #(.select(3), .enable("false")) decoder_2 (
    .out1(decoder_2_out1), .out2(decoder_2_out2), .out4(decoder_2_out4), .sel(n18bitscomparator_1_out));  // open: out0, out3, out5, out6, out7
  and and_1 (and_1_out, decoder_1_out2, decoder_2_out1);
  and and_2 (and_2_out, decoder_1_out1, decoder_2_out4);
  and and_3 (and_3_out, decoder_1_out4, decoder_2_out2);
  and and_4 (and_4_out, decoder_1_out6, decoder_2_out2);
  and and_5 (and_5_out, decoder_1_out6, decoder_2_out1);
  and and_6 (and_6_out, decoder_1_out3, decoder_2_out4);
  and and_7 (and_7_out, decoder_1_out3, decoder_2_out1);
  or or_1 (or_1_out, and_4_out, and_5_out);
  or or_2 (or_2_out, and_6_out, and_7_out);
  or or_3 (BranchOut, and_1_out, and_2_out, and_3_out, or_1_out, or_2_out);
endmodule

// FC
module FullComparator (
  input  a,
  input  b,
  input  eq_in,
  input  gt_in,
  input  lt_in,
  output eq_out,
  output gt_out,
  output lt_out
);

  wire and_1_out, and_2_out, not_1_out, not_2_out, xnor_1_out;

  not not_1 (not_1_out, b);
  not not_2 (not_2_out, a);
  xnor xnor_1 (xnor_1_out, a, b);
  and and_1 (and_1_out, eq_in, a, not_1_out);
  and and_2 (and_2_out, eq_in, not_2_out, b);
  and and_3 (eq_out, xnor_1_out, eq_in);
  or or_1 (gt_out, gt_in, and_1_out);
  or or_2 (lt_out, lt_in, and_2_out);
endmodule

// HC
module HalfComparator (
  input  a,
  input  b,
  output eq,
  output gt,
  output lt
);

  wire not_1_out, not_2_out;

  not not_1 (not_1_out, b);
  not not_2 (not_2_out, a);
  xnor xnor_1 (eq, a, b);
  and and_1 (gt, a, not_1_out);
  and and_2 (lt, not_2_out, b);
endmodule

// Comp
module _18BitsComparator (
  input  [17:0] A,
  input  [17:0] B,
  output [2:0] Out,
  output eq_out,
  output gt_out,
  output lt_out
);

  wire fullcomparator_1_eq_out, fullcomparator_1_gt_out, fullcomparator_1_lt_out, fullcomparator_2_eq_out,
       fullcomparator_2_gt_out, fullcomparator_2_lt_out, fullcomparator_3_eq_out, fullcomparator_3_gt_out,
       fullcomparator_3_lt_out, fullcomparator_4_eq_out, fullcomparator_4_gt_out, fullcomparator_4_lt_out,
       fullcomparator_5_eq_out, fullcomparator_5_gt_out, fullcomparator_5_lt_out, fullcomparator_6_eq_out,
       fullcomparator_6_gt_out, fullcomparator_6_lt_out, fullcomparator_7_eq_out, fullcomparator_7_gt_out,
       fullcomparator_7_lt_out, fullcomparator_8_eq_out, fullcomparator_8_gt_out, fullcomparator_8_lt_out,
       fullcomparator_9_eq_out, fullcomparator_9_gt_out, fullcomparator_9_lt_out, fullcomparator_10_eq_out,
       fullcomparator_10_gt_out, fullcomparator_10_lt_out, fullcomparator_11_eq_out,
       fullcomparator_11_gt_out, fullcomparator_11_lt_out, fullcomparator_12_eq_out,
       fullcomparator_12_gt_out, fullcomparator_12_lt_out, fullcomparator_13_eq_out,
       fullcomparator_13_gt_out, fullcomparator_13_lt_out, fullcomparator_14_eq_out,
       fullcomparator_14_gt_out, fullcomparator_14_lt_out, fullcomparator_15_eq_out,
       fullcomparator_15_gt_out, fullcomparator_15_lt_out, fullcomparator_16_eq_out,
       fullcomparator_16_gt_out, fullcomparator_16_lt_out, halfcomparator_1_eq, halfcomparator_1_gt,
       halfcomparator_1_lt;

  HalfComparator halfcomparator_1 (
    .a(A[17]), .b(B[17]), .eq(halfcomparator_1_eq), .gt(halfcomparator_1_gt), .lt(halfcomparator_1_lt));
  FullComparator fullcomparator_1 (
    .a(A[16]), .b(B[16]), .eq_in(halfcomparator_1_eq), .gt_in(halfcomparator_1_gt),
    .lt_in(halfcomparator_1_lt), .eq_out(fullcomparator_1_eq_out), .gt_out(fullcomparator_1_gt_out),
    .lt_out(fullcomparator_1_lt_out));
  FullComparator fullcomparator_2 (
    .a(A[15]), .b(B[15]), .eq_in(fullcomparator_1_eq_out), .gt_in(fullcomparator_1_gt_out),
    .lt_in(fullcomparator_1_lt_out), .eq_out(fullcomparator_2_eq_out), .gt_out(fullcomparator_2_gt_out),
    .lt_out(fullcomparator_2_lt_out));
  FullComparator fullcomparator_3 (
    .a(A[14]), .b(B[14]), .eq_in(fullcomparator_2_eq_out), .gt_in(fullcomparator_2_gt_out),
    .lt_in(fullcomparator_2_lt_out), .eq_out(fullcomparator_3_eq_out), .gt_out(fullcomparator_3_gt_out),
    .lt_out(fullcomparator_3_lt_out));
  FullComparator fullcomparator_4 (
    .a(A[12]), .b(B[12]), .eq_in(fullcomparator_5_eq_out), .gt_in(fullcomparator_5_gt_out),
    .lt_in(fullcomparator_5_lt_out), .eq_out(fullcomparator_4_eq_out), .gt_out(fullcomparator_4_gt_out),
    .lt_out(fullcomparator_4_lt_out));
  FullComparator fullcomparator_5 (
    .a(A[13]), .b(B[13]), .eq_in(fullcomparator_3_eq_out), .gt_in(fullcomparator_3_gt_out),
    .lt_in(fullcomparator_3_lt_out), .eq_out(fullcomparator_5_eq_out), .gt_out(fullcomparator_5_gt_out),
    .lt_out(fullcomparator_5_lt_out));
  FullComparator fullcomparator_6 (
    .a(A[11]), .b(B[11]), .eq_in(fullcomparator_4_eq_out), .gt_in(fullcomparator_4_gt_out),
    .lt_in(fullcomparator_4_lt_out), .eq_out(fullcomparator_6_eq_out), .gt_out(fullcomparator_6_gt_out),
    .lt_out(fullcomparator_6_lt_out));
  FullComparator fullcomparator_7 (
    .a(A[10]), .b(B[10]), .eq_in(fullcomparator_6_eq_out), .gt_in(fullcomparator_6_gt_out),
    .lt_in(fullcomparator_6_lt_out), .eq_out(fullcomparator_7_eq_out), .gt_out(fullcomparator_7_gt_out),
    .lt_out(fullcomparator_7_lt_out));
  FullComparator fullcomparator_8 (
    .a(A[9]), .b(B[9]), .eq_in(fullcomparator_7_eq_out), .gt_in(fullcomparator_7_gt_out),
    .lt_in(fullcomparator_7_lt_out), .eq_out(fullcomparator_8_eq_out), .gt_out(fullcomparator_8_gt_out),
    .lt_out(fullcomparator_8_lt_out));
  FullComparator fullcomparator_9 (
    .a(A[8]), .b(B[8]), .eq_in(fullcomparator_8_eq_out), .gt_in(fullcomparator_8_gt_out),
    .lt_in(fullcomparator_8_lt_out), .eq_out(fullcomparator_9_eq_out), .gt_out(fullcomparator_9_gt_out),
    .lt_out(fullcomparator_9_lt_out));
  FullComparator fullcomparator_10 (
    .a(A[7]), .b(B[7]), .eq_in(fullcomparator_9_eq_out), .gt_in(fullcomparator_9_gt_out),
    .lt_in(fullcomparator_9_lt_out), .eq_out(fullcomparator_10_eq_out), .gt_out(fullcomparator_10_gt_out),
    .lt_out(fullcomparator_10_lt_out));
  FullComparator fullcomparator_11 (
    .a(A[6]), .b(B[6]), .eq_in(fullcomparator_10_eq_out), .gt_in(fullcomparator_10_gt_out),
    .lt_in(fullcomparator_10_lt_out), .eq_out(fullcomparator_11_eq_out), .gt_out(fullcomparator_11_gt_out),
    .lt_out(fullcomparator_11_lt_out));
  FullComparator fullcomparator_12 (
    .a(A[4]), .b(B[4]), .eq_in(fullcomparator_13_eq_out), .gt_in(fullcomparator_13_gt_out),
    .lt_in(fullcomparator_13_lt_out), .eq_out(fullcomparator_12_eq_out), .gt_out(fullcomparator_12_gt_out),
    .lt_out(fullcomparator_12_lt_out));
  FullComparator fullcomparator_13 (
    .a(A[5]), .b(B[5]), .eq_in(fullcomparator_11_eq_out), .gt_in(fullcomparator_11_gt_out),
    .lt_in(fullcomparator_11_lt_out), .eq_out(fullcomparator_13_eq_out), .gt_out(fullcomparator_13_gt_out),
    .lt_out(fullcomparator_13_lt_out));
  FullComparator fullcomparator_14 (
    .a(A[3]), .b(B[3]), .eq_in(fullcomparator_12_eq_out), .gt_in(fullcomparator_12_gt_out),
    .lt_in(fullcomparator_12_lt_out), .eq_out(fullcomparator_14_eq_out), .gt_out(fullcomparator_14_gt_out),
    .lt_out(fullcomparator_14_lt_out));
  FullComparator fullcomparator_15 (
    .a(A[2]), .b(B[2]), .eq_in(fullcomparator_14_eq_out), .gt_in(fullcomparator_14_gt_out),
    .lt_in(fullcomparator_14_lt_out), .eq_out(fullcomparator_15_eq_out), .gt_out(fullcomparator_15_gt_out),
    .lt_out(fullcomparator_15_lt_out));
  FullComparator fullcomparator_16 (
    .a(A[1]), .b(B[1]), .eq_in(fullcomparator_15_eq_out), .gt_in(fullcomparator_15_gt_out),
    .lt_in(fullcomparator_15_lt_out), .eq_out(fullcomparator_16_eq_out), .gt_out(fullcomparator_16_gt_out),
    .lt_out(fullcomparator_16_lt_out));
  FullComparator fullcomparator_17 (
    .a(A[0]), .b(B[0]), .eq_in(fullcomparator_16_eq_out), .gt_in(fullcomparator_16_gt_out),
    .lt_in(fullcomparator_16_lt_out), .eq_out(eq_out), .gt_out(gt_out), .lt_out(lt_out));

  assign Out = {lt_out, gt_out, eq_out};
endmodule

// PC
module ProgramCounter (
  input  [17:0] JmpAddress,
  input  PCWrite,
  input  Reset,
  input  PC_Read,
  input  Clk,
  output CarryOut,
  output [17:0] Out
);

  wire multiplexer_1_out, multiplexer_2_out, multiplexer_3_out, multiplexer_4_out, multiplexer_5_out,
       multiplexer_6_out, multiplexer_7_out, multiplexer_8_out, multiplexer_9_out, multiplexer_10_out,
       multiplexer_11_out, multiplexer_12_out, multiplexer_13_out, multiplexer_14_out, multiplexer_15_out,
       multiplexer_16_out, multiplexer_17_out, multiplexer_18_out;
  wire [17:0] adder_1_out;

  Multiplexer #(.select(2), .enable("false")) multiplexer_1 (
    .in0(adder_1_out[17]), .in1(JmpAddress[17]), .in2(1'b0), .in3(1'b0), .out(multiplexer_1_out),
    .sel({Reset, PCWrite}));
  D_Flip_Flop d_ff_1 (.clk(Clk), .D(multiplexer_1_out), .Q(Out[17]), .en(PC_Read));  // open: Qn, preset, reset
  Multiplexer #(.select(2), .enable("false")) multiplexer_2 (
    .in0(adder_1_out[16]), .in1(JmpAddress[16]), .in2(1'b0), .in3(1'b0), .out(multiplexer_2_out),
    .sel({Reset, PCWrite}));
  D_Flip_Flop d_ff_2 (.clk(Clk), .D(multiplexer_2_out), .Q(Out[16]), .en(PC_Read));  // open: Qn, preset, reset
  Multiplexer #(.select(2), .enable("false")) multiplexer_3 (
    .in0(adder_1_out[15]), .in1(JmpAddress[15]), .in2(1'b0), .in3(1'b0), .out(multiplexer_3_out),
    .sel({Reset, PCWrite}));
  Multiplexer #(.select(2), .enable("false")) multiplexer_4 (
    .in0(adder_1_out[14]), .in1(JmpAddress[14]), .in2(1'b0), .in3(1'b0), .out(multiplexer_4_out),
    .sel({Reset, PCWrite}));
  D_Flip_Flop d_ff_3 (.clk(Clk), .D(multiplexer_3_out), .Q(Out[15]), .en(PC_Read));  // open: Qn, preset, reset
  Multiplexer #(.select(2), .enable("false")) multiplexer_5 (
    .in0(adder_1_out[13]), .in1(JmpAddress[13]), .in2(1'b0), .in3(1'b0), .out(multiplexer_5_out),
    .sel({Reset, PCWrite}));
  D_Flip_Flop d_ff_4 (.clk(Clk), .D(multiplexer_4_out), .Q(Out[14]), .en(PC_Read));  // open: Qn, preset, reset
  D_Flip_Flop d_ff_5 (.D(multiplexer_5_out), .Q(Out[13]), .en(PC_Read));  // open: clk, Qn, preset, reset
  Multiplexer #(.select(2), .enable("false")) multiplexer_6 (
    .in0(adder_1_out[12]), .in1(JmpAddress[12]), .in2(1'b0), .in3(1'b0), .out(multiplexer_6_out),
    .sel({Reset, PCWrite}));
  Multiplexer #(.select(2), .enable("false")) multiplexer_7 (
    .in0(adder_1_out[11]), .in1(JmpAddress[11]), .in2(1'b0), .in3(1'b0), .out(multiplexer_7_out),
    .sel({Reset, PCWrite}));
  D_Flip_Flop d_ff_6 (.clk(Clk), .D(multiplexer_6_out), .Q(Out[12]), .en(PC_Read));  // open: Qn, preset, reset
  D_Flip_Flop d_ff_7 (.clk(Clk), .D(multiplexer_7_out), .Q(Out[11]), .en(PC_Read));  // open: Qn, preset, reset
  Multiplexer #(.select(2), .enable("false")) multiplexer_8 (
    .in0(adder_1_out[10]), .in1(JmpAddress[10]), .in2(1'b0), .in3(1'b0), .out(multiplexer_8_out),
    .sel({Reset, PCWrite}));
  D_Flip_Flop d_ff_8 (.clk(Clk), .D(multiplexer_8_out), .Q(Out[10]), .en(PC_Read));  // open: Qn, preset, reset
  Multiplexer #(.select(2), .enable("false")) multiplexer_9 (
    .in0(adder_1_out[9]), .in1(JmpAddress[9]), .in2(1'b0), .in3(1'b0), .out(multiplexer_9_out),
    .sel({Reset, PCWrite}));
  Multiplexer #(.select(2), .enable("false")) multiplexer_10 (
    .in0(adder_1_out[8]), .in1(JmpAddress[8]), .in2(1'b0), .in3(1'b0), .out(multiplexer_10_out),
    .sel({Reset, PCWrite}));
  D_Flip_Flop d_ff_9 (.clk(Clk), .D(multiplexer_9_out), .Q(Out[9]), .en(PC_Read));  // open: Qn, preset, reset
  D_Flip_Flop d_ff_10 (.clk(Clk), .D(multiplexer_10_out), .Q(Out[8]), .en(PC_Read));  // open: Qn, preset, reset
  Multiplexer #(.select(2), .enable("false")) multiplexer_11 (
    .in0(adder_1_out[7]), .in1(JmpAddress[7]), .in2(1'b0), .in3(1'b0), .out(multiplexer_11_out),
    .sel({Reset, PCWrite}));
  D_Flip_Flop d_ff_11 (.clk(Clk), .D(multiplexer_11_out), .Q(Out[7]), .en(PC_Read));  // open: Qn, preset, reset
  Multiplexer #(.select(2), .enable("false")) multiplexer_12 (
    .in0(adder_1_out[6]), .in1(JmpAddress[6]), .in2(1'b0), .in3(1'b0), .out(multiplexer_12_out),
    .sel({Reset, PCWrite}));
  Multiplexer #(.select(2), .enable("false")) multiplexer_13 (
    .in0(adder_1_out[5]), .in1(JmpAddress[5]), .in2(1'b0), .in3(1'b0), .out(multiplexer_13_out),
    .sel({Reset, PCWrite}));
  D_Flip_Flop d_ff_12 (.clk(Clk), .D(multiplexer_12_out), .Q(Out[6]), .en(PC_Read));  // open: Qn, preset, reset
  D_Flip_Flop d_ff_13 (.clk(Clk), .D(multiplexer_13_out), .Q(Out[5]), .en(PC_Read));  // open: Qn, preset, reset
  Multiplexer #(.select(2), .enable("false")) multiplexer_14 (
    .in0(adder_1_out[4]), .in1(JmpAddress[4]), .in2(1'b0), .in3(1'b0), .out(multiplexer_14_out),
    .sel({Reset, PCWrite}));
  Multiplexer #(.select(2), .enable("false")) multiplexer_15 (
    .in0(adder_1_out[3]), .in1(JmpAddress[3]), .in2(1'b0), .in3(1'b0), .out(multiplexer_15_out),
    .sel({Reset, PCWrite}));
  D_Flip_Flop d_ff_14 (.clk(Clk), .D(multiplexer_14_out), .Q(Out[4]), .en(PC_Read));  // open: Qn, preset, reset
  D_Flip_Flop d_ff_15 (.clk(Clk), .D(multiplexer_15_out), .Q(Out[3]), .en(PC_Read));  // open: Qn, preset, reset
  Multiplexer #(.select(2), .enable("false")) multiplexer_16 (
    .in0(adder_1_out[2]), .in1(JmpAddress[2]), .in2(1'b0), .in3(1'b0), .out(multiplexer_16_out),
    .sel({Reset, PCWrite}));
  D_Flip_Flop d_ff_16 (.clk(Clk), .D(multiplexer_16_out), .Q(Out[2]), .en(PC_Read));  // open: Qn, preset, reset
  Multiplexer #(.select(2), .enable("false")) multiplexer_17 (
    .in0(adder_1_out[1]), .in1(JmpAddress[1]), .in2(1'b0), .in3(1'b0), .out(multiplexer_17_out),
    .sel({Reset, PCWrite}));
  Multiplexer #(.select(2), .enable("false")) multiplexer_18 (
    .in0(adder_1_out[0]), .in1(JmpAddress[0]), .in2(1'b0), .in3(1'b0), .out(multiplexer_18_out),
    .sel({Reset, PCWrite}));
  D_Flip_Flop d_ff_17 (.clk(Clk), .D(multiplexer_17_out), .Q(Out[1]), .en(PC_Read));  // open: Qn, preset, reset
  D_Flip_Flop d_ff_18 (.clk(Clk), .D(multiplexer_18_out), .Q(Out[0]), .en(PC_Read));  // open: Qn, preset, reset
  Adder #(.width(18)) adder_1 (.a(18'h1), .b(Out), .out(adder_1_out), .cout(CarryOut));  // open: cin
endmodule

// Reg
module Registers (
  input  [17:0] Input_Data,
  input  [3:0] Src1,
  input  [3:0] Src2,
  input  [3:0] DST,
  input  Reset,
  input  Load,
  input  Clock,
  output [17:0] SRC1_2,
  output [17:0] SRC2_2
);

  wire and_1_out, and_2_out, and_3_out, and_4_out, and_5_out, and_6_out, and_7_out, and_8_out, and_9_out,
       and_10_out, and_11_out, and_12_out, and_13_out, and_14_out, and_15_out, and_16_out, decoder_1_out0,
       decoder_1_out1, decoder_1_out2, decoder_1_out3, decoder_1_out4, decoder_1_out5, decoder_1_out6,
       decoder_1_out7, decoder_1_out8, decoder_1_out9, decoder_1_out10, decoder_1_out11, decoder_1_out12,
       decoder_1_out13, decoder_1_out14, decoder_1_out15;
  wire [17:0] register_1_q, register_2_q, register_3_q, register_4_q, register_5_q, register_6_q,
       register_7_q, register_8_q, register_9_q, register_10_q, register_11_q, register_12_q, register_13_q,
       register_14_q, register_15_q, register_16_q;

  Decoder #(.select(4)) decoder_1 (
    .out0(decoder_1_out0), .out1(decoder_1_out1), .out2(decoder_1_out2), .out3(decoder_1_out3),
    .out4(decoder_1_out4), .out5(decoder_1_out5), .out6(decoder_1_out6), .out7(decoder_1_out7),
    .out8(decoder_1_out8), .out9(decoder_1_out9), .out10(decoder_1_out10), .out11(decoder_1_out11),
    .out12(decoder_1_out12), .out13(decoder_1_out13), .out14(decoder_1_out14), .out15(decoder_1_out15),
    .sel(DST));  // open: en
  and and_1 (and_1_out, decoder_1_out0, Load);
  and and_2 (and_2_out, decoder_1_out1, Load);
  and and_3 (and_3_out, decoder_1_out2, Load);
  and and_4 (and_4_out, decoder_1_out3, Load);
  and and_5 (and_5_out, decoder_1_out4, Load);
  and and_6 (and_6_out, decoder_1_out5, Load);
  and and_7 (and_7_out, decoder_1_out6, Load);
  and and_8 (and_8_out, decoder_1_out7, Load);
  Register #(.width(18)) register_1 (.D(Input_Data), .en(and_1_out), .Q(register_1_q), .clk(Clock), .clr(Reset));
  Register #(.width(18)) register_2 (.D(Input_Data), .en(and_2_out), .Q(register_2_q), .clk(Clock), .clr(Reset));
  Register #(.width(18)) register_3 (.D(Input_Data), .en(and_3_out), .Q(register_3_q), .clk(Clock), .clr(Reset));
  Register #(.width(18)) register_4 (.D(Input_Data), .en(and_4_out), .Q(register_4_q), .clk(Clock), .clr(Reset));
  Register #(.width(18)) register_5 (.D(Input_Data), .en(and_5_out), .Q(register_5_q), .clk(Clock), .clr(Reset));
  Register #(.width(18)) register_6 (.D(Input_Data), .en(and_6_out), .Q(register_6_q), .clk(Clock), .clr(Reset));
  Register #(.width(18)) register_7 (.D(Input_Data), .en(and_7_out), .Q(register_7_q), .clk(Clock), .clr(Reset));
  Register #(.width(18)) register_8 (.D(Input_Data), .en(and_8_out), .Q(register_8_q), .clk(Clock), .clr(Reset));
  and and_9 (and_9_out, decoder_1_out8, Load);
  and and_10 (and_10_out, decoder_1_out9, Load);
  and and_11 (and_11_out, decoder_1_out10, Load);
  and and_12 (and_12_out, decoder_1_out11, Load);
  and and_13 (and_13_out, decoder_1_out12, Load);
  and and_14 (and_14_out, decoder_1_out13, Load);
  and and_15 (and_15_out, decoder_1_out14, Load);
  and and_16 (and_16_out, decoder_1_out15, Load);
  Register #(.width(18)) register_9 (.D(Input_Data), .en(and_9_out), .Q(register_9_q), .clk(Clock), .clr(Reset));
  Register #(.width(18)) register_10 (.D(Input_Data), .en(and_10_out), .Q(register_10_q), .clk(Clock), .clr(Reset));
  Register #(.width(18)) register_11 (.en(and_11_out), .Q(register_11_q), .clk(Clock), .clr(Reset));  // open: D
  Register #(.width(18)) register_12 (.D(Input_Data), .en(and_12_out), .Q(register_12_q), .clk(Clock), .clr(Reset));
  Register #(.width(18)) register_13 (.D(Input_Data), .en(and_13_out), .Q(register_13_q), .clk(Clock), .clr(Reset));
  Register #(.width(18)) register_14 (.D(Input_Data), .en(and_14_out), .Q(register_14_q), .clk(Clock), .clr(Reset));
  Register #(.width(18)) register_15 (.D(Input_Data), .en(and_15_out), .Q(register_15_q), .clk(Clock), .clr(Reset));
  Register #(.width(18)) register_16 (.D(Input_Data), .en(and_16_out), .Q(register_16_q), .clk(Clock), .clr(Reset));
  Multiplexer #(.select(4), .width(18), .enable("false")) multiplexer_1 (
    .in0(register_1_q), .in1(register_2_q), .in2(register_3_q), .in3(register_4_q), .in4(register_5_q),
    .in5(register_6_q), .in6(register_7_q), .in7(register_8_q), .in8(register_9_q), .in9(register_10_q),
    .in10(register_11_q), .in11(register_12_q), .in12(register_13_q), .in13(register_14_q),
    .in14(register_15_q), .in15(register_16_q), .out(SRC1_2), .sel(Src1));
  Multiplexer #(.select(4), .width(18), .enable("false")) multiplexer_2 (
    .in0(register_1_q), .in1(register_2_q), .in2(register_3_q), .in3(register_4_q), .in4(register_5_q),
    .in5(register_6_q), .in6(register_7_q), .in7(register_8_q), .in8(register_9_q), .in9(register_10_q),
    .in10(register_11_q), .in11(register_12_q), .in12(register_13_q), .in13(register_14_q),
    .in14(register_15_q), .in15(register_16_q), .out(SRC2_2), .sel(Src2));
endmodule

module Control_Unit (
  input  [17:0] Instruction,
  input  CounterReset,
  input  Clock,
  output [5:0] IMM6,
  output [3:0] SR2_OP2,
  output [3:0] SR1_OP1,
  output [3:0] DSR,
  output [2:0] NZP,
  output [17:0] ADDR,
  output Load_Active,
  output Jmp_Enable,
  output Br_Enable,
  output PC_Read,
  output Fetch_Inst,
  output Register_Read,
  output DataMem_Read,
  output PC_Write,
  output ALU_Enable,
  output Register_Write,
  output DataMem_Write,
  output Select_IMM,
  output [3:0] Operation_Select,
  output Reset_State
);

  wire and_1_out, and_2_out, and_3_out, and_5_out, and_6_out, and_8_out, and_10_out, decoder_1_out0,
       decoder_1_out1, decoder_1_out2, decoder_1_out4, decoder_1_out5, decoder_1_out6, decoder_1_out7,
       decoder_1_out8, decoder_1_out9, decoder_1_out11, decoder_1_out12, decoder_1_out13, decoder_1_out14,
       decoder_1_out15, decoder_2_out2, decoder_2_out3, decoder_2_out4, or_1_out, or_7_out;
  wire [0:0] or_9_out;
  wire [2:0] counter3_1_out;
  wire [17:0] signextender14_1_signextended, zeroextender3_1_zeroextended, zeroextender10_1_zeroextended;

  Decoder #(.select(4), .enable("false")) decoder_1 (
    .out0(decoder_1_out0), .out1(decoder_1_out1), .out2(decoder_1_out2), .out3(Load_Active),
    .out4(decoder_1_out4), .out5(decoder_1_out5), .out6(decoder_1_out6), .out7(decoder_1_out7),
    .out8(decoder_1_out8), .out9(decoder_1_out9), .out10(Jmp_Enable), .out11(decoder_1_out11),
    .out12(decoder_1_out12), .out13(decoder_1_out13), .out14(decoder_1_out14), .out15(decoder_1_out15),
    .sel(Instruction[17:14]));
  or or_1 (or_1_out, Reset_State, CounterReset);
  Counter3 counter3_1 (.Reset(or_1_out), .Clk(Clock), .Out(counter3_1_out));  // open: CarryOut
  Decoder #(.select(3), .enable("false")) decoder_2 (
    .out0(PC_Read), .out1(Fetch_Inst), .out2(decoder_2_out2), .out3(decoder_2_out3), .out4(decoder_2_out4),
    .out5(Reset_State), .sel(counter3_1_out));  // open: out6, out7
  or or_2 (Br_Enable, decoder_1_out11, decoder_1_out12, decoder_1_out13, decoder_1_out14, decoder_1_out15);
  or or_3 (Operation_Select[3], decoder_1_out5, decoder_1_out0);
  or or_4 (Operation_Select[2], decoder_1_out6, decoder_1_out1);
  or or_5 (Operation_Select[0], decoder_1_out7, decoder_1_out2);
  or or_6 (Operation_Select[1], decoder_1_out9, decoder_1_out8);
  or or_7 (or_7_out, decoder_1_out0, decoder_1_out1, decoder_1_out2, decoder_1_out5, decoder_1_out6, decoder_1_out7, decoder_1_out8, decoder_1_out9);
  and and_1 (and_1_out, Br_Enable, decoder_2_out2);
  and and_2 (and_2_out, or_7_out, decoder_2_out2);
  and and_3 (and_3_out, decoder_1_out4, decoder_2_out2);
  and and_4 (DataMem_Read, Load_Active, decoder_2_out2);
  and and_5 (and_5_out, Br_Enable, decoder_2_out2);
  and and_6 (and_6_out, Jmp_Enable, decoder_2_out2);
  and and_7 (ALU_Enable, or_7_out, decoder_2_out3);
  and and_8 (and_8_out, Load_Active, decoder_2_out3);
  and and_9 (DataMem_Write, decoder_1_out4, decoder_2_out3);
  and and_10 (and_10_out, or_7_out, decoder_2_out4);
  or or_8 (Select_IMM, decoder_1_out5, decoder_1_out6, decoder_1_out7, decoder_1_out9);
  Multiplexer #(.width(4), .enable("false")) multiplexer_1 (
    .in0(Instruction[9:6]), .in1(Instruction[13:10]), .out(SR1_OP1), .sel(decoder_1_out4));
  or or_9 (or_9_out[0], Load_Active, decoder_1_out4);
  ZeroExtender10 zeroextender10_1 (.\İnput (Instruction[9:0]), .ZeroExtended(zeroextender10_1_zeroextended));
  SignExtender14 signextender14_1 (.\İnput (Instruction[13:0]), .SignExtended(signextender14_1_signextended));
  ZeroExtender3 zeroextender3_1 (
    .\İnput ({Instruction[13], Instruction[5:4]}), .ZeroExtended(zeroextender3_1_zeroextended));
  or or_10 (Register_Read, and_2_out, and_1_out, and_3_out);
  or or_11 (PC_Write, and_5_out, and_6_out);
  or or_12 (Register_Write, and_8_out, and_10_out);
  Multiplexer #(.select(3), .width(18), .enable("false")) multiplexer_2 (
    .in0({18{1'b0}}), .in1(zeroextender10_1_zeroextended), .in2(signextender14_1_signextended),
    .in4(zeroextender3_1_zeroextended), .out(ADDR), .sel({Br_Enable, Jmp_Enable, or_9_out[0]}));  // open: in3, in5, in6, in7

  assign DSR = Instruction[13:10];
  assign IMM6 = {Instruction[4], Instruction[5], Instruction[3:0]};
  assign NZP = Instruction[12:10];
  assign SR2_OP2 = Instruction[3:0];

  // Notes on the sheet:
  //   Operation Detector
  //   State Detector
  //   AND/ANDI
  //   OR/ORI
  //   ADD/ADDI
  //   XOR/XORI
endmodule

module Counter (
  input  Reset,
  input  Clk,
  output CarryOut,
  output [17:0] Out
);

  wire multiplexer_1_out, multiplexer_2_out, multiplexer_3_out, multiplexer_4_out, multiplexer_5_out,
       multiplexer_6_out, multiplexer_7_out, multiplexer_8_out, multiplexer_9_out, multiplexer_10_out,
       multiplexer_11_out, multiplexer_12_out, multiplexer_13_out, multiplexer_14_out, multiplexer_15_out,
       multiplexer_16_out, multiplexer_17_out, multiplexer_18_out;
  wire [17:0] adder_1_out;

  Multiplexer #(.enable("false")) multiplexer_1 (
    .in0(adder_1_out[17]), .in1(1'b0), .out(multiplexer_1_out), .sel(Reset));
  D_Flip_Flop d_ff_1 (.clk(Clk), .D(multiplexer_1_out), .Q(Out[17]));  // open: Qn, preset, en, reset
  Multiplexer #(.enable("false")) multiplexer_2 (
    .in0(adder_1_out[16]), .in1(1'b0), .out(multiplexer_2_out), .sel(Reset));
  D_Flip_Flop d_ff_2 (.clk(Clk), .D(multiplexer_2_out), .Q(Out[16]));  // open: Qn, preset, en, reset
  Multiplexer #(.enable("false")) multiplexer_3 (
    .in0(adder_1_out[15]), .in1(1'b0), .out(multiplexer_3_out), .sel(Reset));
  Multiplexer #(.enable("false")) multiplexer_4 (
    .in0(adder_1_out[14]), .in1(1'b0), .out(multiplexer_4_out), .sel(Reset));
  D_Flip_Flop d_ff_3 (.clk(Clk), .D(multiplexer_3_out), .Q(Out[15]));  // open: Qn, preset, en, reset
  Multiplexer #(.enable("false")) multiplexer_5 (
    .in0(adder_1_out[13]), .in1(1'b0), .out(multiplexer_5_out), .sel(Reset));
  D_Flip_Flop d_ff_4 (.clk(Clk), .D(multiplexer_4_out), .Q(Out[14]));  // open: Qn, preset, en, reset
  D_Flip_Flop d_ff_5 (.D(multiplexer_5_out), .Q(Out[13]));  // open: clk, Qn, preset, en, reset
  Multiplexer #(.enable("false")) multiplexer_6 (
    .in0(adder_1_out[12]), .in1(1'b0), .out(multiplexer_6_out), .sel(Reset));
  Multiplexer #(.enable("false")) multiplexer_7 (
    .in0(adder_1_out[11]), .in1(1'b0), .out(multiplexer_7_out), .sel(Reset));
  D_Flip_Flop d_ff_6 (.clk(Clk), .D(multiplexer_6_out), .Q(Out[12]));  // open: Qn, preset, en, reset
  D_Flip_Flop d_ff_7 (.clk(Clk), .D(multiplexer_7_out), .Q(Out[11]));  // open: Qn, preset, en, reset
  Multiplexer #(.enable("false")) multiplexer_8 (
    .in0(adder_1_out[10]), .in1(1'b0), .out(multiplexer_8_out), .sel(Reset));
  D_Flip_Flop d_ff_8 (.clk(Clk), .D(multiplexer_8_out), .Q(Out[10]));  // open: Qn, preset, en, reset
  Multiplexer #(.enable("false")) multiplexer_9 (
    .in0(adder_1_out[9]), .in1(1'b0), .out(multiplexer_9_out), .sel(Reset));
  Multiplexer #(.enable("false")) multiplexer_10 (
    .in0(adder_1_out[8]), .in1(1'b0), .out(multiplexer_10_out), .sel(Reset));
  D_Flip_Flop d_ff_9 (.clk(Clk), .D(multiplexer_9_out), .Q(Out[9]));  // open: Qn, preset, en, reset
  D_Flip_Flop d_ff_10 (.clk(Clk), .D(multiplexer_10_out), .Q(Out[8]));  // open: Qn, preset, en, reset
  Multiplexer #(.enable("false")) multiplexer_11 (
    .in0(adder_1_out[7]), .in1(1'b0), .out(multiplexer_11_out), .sel(Reset));
  D_Flip_Flop d_ff_11 (.clk(Clk), .D(multiplexer_11_out), .Q(Out[7]));  // open: Qn, preset, en, reset
  Multiplexer #(.enable("false")) multiplexer_12 (
    .in0(adder_1_out[6]), .in1(1'b0), .out(multiplexer_12_out), .sel(Reset));
  Multiplexer #(.enable("false")) multiplexer_13 (
    .in0(adder_1_out[5]), .in1(1'b0), .out(multiplexer_13_out), .sel(Reset));
  D_Flip_Flop d_ff_12 (.clk(Clk), .D(multiplexer_12_out), .Q(Out[6]));  // open: Qn, preset, en, reset
  D_Flip_Flop d_ff_13 (.clk(Clk), .D(multiplexer_13_out), .Q(Out[5]));  // open: Qn, preset, en, reset
  Multiplexer #(.enable("false")) multiplexer_14 (
    .in0(adder_1_out[4]), .in1(1'b0), .out(multiplexer_14_out), .sel(Reset));
  Multiplexer #(.enable("false")) multiplexer_15 (
    .in0(adder_1_out[3]), .in1(1'b0), .out(multiplexer_15_out), .sel(Reset));
  D_Flip_Flop d_ff_14 (.clk(Clk), .D(multiplexer_14_out), .Q(Out[4]));  // open: Qn, preset, en, reset
  D_Flip_Flop d_ff_15 (.clk(Clk), .D(multiplexer_15_out), .Q(Out[3]));  // open: Qn, preset, en, reset
  Multiplexer #(.enable("false")) multiplexer_16 (
    .in0(adder_1_out[2]), .in1(1'b0), .out(multiplexer_16_out), .sel(Reset));
  D_Flip_Flop d_ff_16 (.clk(Clk), .D(multiplexer_16_out), .Q(Out[2]));  // open: Qn, preset, en, reset
  Multiplexer #(.enable("false")) multiplexer_17 (
    .in0(adder_1_out[1]), .in1(1'b0), .out(multiplexer_17_out), .sel(Reset));
  Multiplexer #(.enable("false")) multiplexer_18 (
    .in0(adder_1_out[0]), .in1(1'b0), .out(multiplexer_18_out), .sel(Reset));
  D_Flip_Flop d_ff_17 (.clk(Clk), .D(multiplexer_17_out), .Q(Out[1]));  // open: Qn, preset, en, reset
  D_Flip_Flop d_ff_18 (.clk(Clk), .D(multiplexer_18_out), .Q(Out[0]));  // open: Qn, preset, en, reset
  Adder #(.width(18)) adder_1 (.a(18'h1), .b(Out), .out(adder_1_out), .cout(CarryOut));  // open: cin
endmodule

// Count
module Counter3 (
  input  Reset,
  input  Clk,
  output CarryOut,
  output [2:0] Out
);

  wire multiplexer_1_out, multiplexer_2_out, multiplexer_3_out;
  wire [2:0] adder_1_out;

  Multiplexer #(.enable("false")) multiplexer_1 (
    .in0(adder_1_out[2]), .in1(1'b0), .out(multiplexer_1_out), .sel(Reset));
  D_Flip_Flop d_ff_1 (.clk(Clk), .D(multiplexer_1_out), .Q(Out[2]));  // open: Qn, preset, en, reset
  Multiplexer #(.enable("false")) multiplexer_2 (
    .in0(adder_1_out[1]), .in1(1'b0), .out(multiplexer_2_out), .sel(Reset));
  D_Flip_Flop d_ff_2 (.clk(Clk), .D(multiplexer_2_out), .Q(Out[1]));  // open: Qn, preset, en, reset
  Multiplexer #(.enable("false")) multiplexer_3 (
    .in0(adder_1_out[0]), .in1(1'b0), .out(multiplexer_3_out), .sel(Reset));
  D_Flip_Flop d_ff_3 (.clk(Clk), .D(multiplexer_3_out), .Q(Out[0]));  // open: Qn, preset, en, reset
  Adder #(.width(3)) adder_1 (.a(3'b001), .b(Out), .out(adder_1_out), .cout(CarryOut));  // open: cin
endmodule

// ZE10
module ZeroExtender10 (
  input  [9:0] \İnput ,
  output [17:0] ZeroExtended
);


  assign ZeroExtended = {{8{1'b0}}, \İnput };
endmodule

// SE14
module SignExtender14 (
  input  [13:0] \İnput ,
  output [17:0] SignExtended
);


  assign SignExtended = {{5{\İnput [13]}}, \İnput [12:0]};
endmodule

// ZE3
module ZeroExtender3 (
  input  [2:0] \İnput ,
  output [17:0] ZeroExtended
);


  assign ZeroExtended = {{15{1'b0}}, \İnput };
endmodule

// SE6
module SignExtender6 (
  input  [5:0] \İnput ,
  output [17:0] SignExtended
);


  assign SignExtended = {{13{\İnput [5]}}, \İnput [4:0]};
endmodule
